# Fritzing sketch i2c_LCD (saved by Fritzing 0.9.3b)

parts:
  LCM1602_IIC1 = LCM1602 IIC [part_number="LCM1602 IIC" chip_label="LCM1602 IIC" package="DIP (Dual Inline) [THT]"]
  LCD1 = LCD screen  # not connected
  Part1 = Arduino Uno (Rev3)

nets:
  GND: LCM1602_IIC1.GND, Part1.GND
  VCC: LCM1602_IIC1.VCC, Part1.5V
  N1: LCM1602_IIC1.SDA, Part1.A4/SDA
  N2: LCM1602_IIC1.SCL, Part1.A5/SCL

custom parts:
  LCM1602 IIC: I2C-Module to use a 1602 or 2004 LCD on with the wire.h libory Serial LCD Modul
